# Fritzing sketch RFLink Gatway (saved by Fritzing 0.9.4)
breadboards: 1

parts:
  Part1 = Logic Level Converter [part_number="BSS138 bidirectional logic level converter"]
  R1 = Resistor [tolerance=±5% resistance=471 package="0603 [SMD]"]
  R2 = Resistor [tolerance=±5% resistance=471 package="0603 [SMD]"]
  R3 = Resistor [tolerance=±5% resistance=471 package="0603 [SMD]"]
  R4 = Resistor [tolerance=±5% resistance=471 package="0603 [SMD]"]  # not connected
  U3 = V_REG_MIC2920 [package=sot223]
  Part2 = Arduino Mega 2560 (Rev3)
  SRX882 = female pin header, 4 pins [form="♀ (female)"]
  STX882 = female pin header, 3 pins [form="♀ (female)"]
  CC2500 = female pin header, 8 pins [form="♀ (female)"]
  NodeMCU1 = NodeMCU V1.0 [part_number=A]

nets:
  N1: Part1.TX2_LV, NodeMCU1.RX
  N2: Part1.RX2_LV, NodeMCU1.TX
  GND: Part1.GND, U3.GND, Part2.GND, Part2.D6_PWM, Part2.D7_PWM, SRX882.pin1, STX882.pin1, CC2500.pin7, NodeMCU1.GND
  N3: Part1.LV, U3.OUT, CC2500.pin8
  5V: Part1.HV, U3.IN, Part2.5V, SRX882.pin4, STX882.pin2, NodeMCU1.Vin
  N4: Part1.RX2_HV, Part2.D0_RX0
  N5: Part1.TX2_HV, Part2.D1_TX0
  N6: R1.Pin_0, CC2500.pin6
  N7: R1.Pin_1, Part2.D51
  N8: R2.Pin_0, CC2500.pin5
  N9: R2.Pin_1, Part2.D52
  N10: R3.Pin_0, CC2500.pin4
  N11: R3.Pin_1, Part2.D50
  N12: Part2.D19/RX1, SRX882.pin2
  N13: Part2.D15/RX3, STX882.pin3

notes:
  5V DC
  3.3V DC
  Pin 6 grounded to unlock CC2500 support.
  Pin 7 grounded to disable internal pullup on RF data pin.
  RFLink Wiring Details
  Rev 2.0

custom parts:
  NodeMCU V1.0: ESP8266 based NodeMCU
